# Fritzing sketch Focuser (saved by Fritzing 0.9.3b)

parts:
  Part1 = ESP-WROOM-32 [ESP-32S] Module [part_number=ESP-WROOM-32]
  SM1 = 28BYJ-48 Stepper Motor [part_number=28BYJ-48]
  Driver1 = 28BYJ-48 Driver Module [part_number=ULN2003 package=THT]
  Part2 = Arduino Joystick Shield

nets:
  N1: Part1.IO34, Part2.HORIZONTAL
  N2: Part1.IO35, Part2.VERTICAL
  N3: Part1.IO33, Part2.SEL
  N4: Part1.IO26, Part2.D3
  N5: Part1.IO14, Part2.D4
  N6: Part1.IO13, Part2.D5
  N7: Part1.IO5, Driver1.IN4
  N8: Part1.IO19, Driver1.IN3
  N9: Part1.IO21, Driver1.IN2
  N10: Part1.IO23, Driver1.IN1
  N11: SM1.blue-pin, Driver1.blue-pin
  N12: SM1.pink-pin, Driver1.pink-pin
  N13: SM1.yellow-pin, Driver1.yellow-pin
  N14: SM1.orange-pin, Driver1.orange-pin
  N15: SM1.red-pin, Driver1.red-pin

custom parts:
  ESP-WROOM-32 [ESP-32S] Module: Espressif ESP-WROOM-32 WiFi/Bluetooth LE microcontroller module also known as the Ai-Thinker ESP-32S module with similar formfactor. The ESP32 is a microcontroller chip with WiFi and BLE capabilities. The chip is developed by Espressif and is the successor to the popular ESP8266 WiFi module.
  28BYJ-48 Stepper Motor: Unipolar Stepper Motor 28BYJ-48 Top coil - pink & orange Bottom coil - blue & yellow Common rail - red Connector pins: blue - pink - yellow - orange - red
  28BYJ-48 Driver Module: High-power ULN2003 Stepper Motor Driver Board Test Module For Arduino AVR SMD
